# Fritzing sketch piezo-test-rig (saved by Fritzing 0.9.2b)
breadboards: 1

parts:
  J1 = Piezo Speaker
  Part1 = Arduino Uno (Rev3)
  Part2 = Arduino Uno (Rev3)

nets:
  GND: J1.pin1, Part1.GND, Part2.GND
  N1: J1.pin2, Part1.D3_PWM
  N2: Part1.A4/SDA, Part2.A4/SDA
  N3: Part1.A5/SCL, Part2.A5/SCL
  VIN: Part1.VIN, Part2.5V

notes:
  This one has StandardFirmata on it.
  This one will initially have a "test" program that proves the piezo functions correctly.
  Once that's complete, we'll write and upload a firmware that will turn this one into an I2C slave device that accepts instructions via the I2C bus and translates them into piezo buzz output.
